// Logisim project 152120241075_1.circ as structural Verilog: 2 circuits, main circuit main
module main (
);

  wire clock_1_out, ic_7447_1_a_2, ic_7447_1_b_2, ic_7447_1_c_2, ic_7447_1_d_2, ic_7447_1_e, ic_7447_1_f,
       ic_7447_1_g, ic_7493_1_p2, ic_7493_1_p7, ic_7493_1_p8, ic_7493_1_p9;

  Clock clock_1 (.out(clock_1_out));
  // IC_7493 ic_7493_1: pin names not known; wires that end beside it: clock_1_out, ic_7493_1_p2, 1'b0, 1'b1, 1'b0, ic_7493_1_p2, ic_7493_1_p7, ic_7493_1_p8, ic_7493_1_p9, 1'b1, 1'b0
  IC_7447 ic_7447_1 (
    .D(ic_7493_1_p9), .C(ic_7493_1_p8), .B(ic_7493_1_p7), .A(ic_7493_1_p2), .a_2(ic_7447_1_a_2),
    .b_2(ic_7447_1_b_2), .c_2(ic_7447_1_c_2), .d_2(ic_7447_1_d_2), .e(ic_7447_1_e), .f(ic_7447_1_f),
    .g(ic_7447_1_g));
  _7_Segment_Display u_7_segment_display_1 (
    .g(ic_7447_1_g), .f(ic_7447_1_f), .a(ic_7447_1_a_2), .b(ic_7447_1_b_2), .e(ic_7447_1_e),
    .d(ic_7447_1_d_2), .c(ic_7447_1_c_2));  // open: dp

  // Notes on the sheet:
  //   D
  //   C
  //   B
  //   A
  //   7447
endmodule

module IC_7447 (
  input  D,
  input  C,
  input  B,
  input  A,
  output a_2,
  output b_2,
  output c_2,
  output d_2,
  output e,
  output f,
  output g
);

  wire and_1_out, and_2_out, and_3_out, and_4_out, and_5_out, and_6_out, and_7_out, and_8_out, and_9_out,
       and_10_out, and_11_out, and_12_out, and_13_out, and_14_out, and_15_out, and_16_out, and_17_out,
       and_18_out, and_19_out, and_20_out, and_21_out, and_22_out, and_23_out, and_24_out, and_25_out,
       and_26_out, and_27_out, and_28_out, and_29_out, not_1_out, not_2_out, not_3_out, not_4_out, not_5_out,
       not_6_out, not_7_out, not_8_out, not_9_out, not_10_out, not_11_out, not_12_out, not_13_out,
       not_14_out, not_15_out, not_16_out, not_17_out, not_18_out, not_19_out, not_20_out, not_21_out,
       not_22_out, not_23_out, not_24_out, not_25_out, not_26_out, not_27_out, not_28_out, not_29_out,
       not_30_out, not_31_out, not_32_out, not_33_out, not_34_out, not_35_out, not_36_out, not_37_out,
       not_38_out, not_39_out, not_40_out, not_41_out, not_42_out, not_43_out;

  not not_1 (not_1_out, D);
  not not_2 (not_2_out, C);
  and and_1 (and_1_out, not_1_out, not_2_out, not_3_out);
  not not_3 (not_3_out, A);
  not not_4 (not_4_out, D);
  not not_5 (not_5_out, C);
  and and_2 (and_2_out, not_4_out, not_5_out, B);
  not not_6 (not_6_out, D);
  and and_3 (and_3_out, not_6_out, C, A);
  not not_7 (not_7_out, C);
  and and_4 (and_4_out, D, not_7_out, not_8_out);
  not not_8 (not_8_out, B);
  not not_9 (not_9_out, D);
  and and_5 (and_5_out, not_9_out, not_10_out);
  not not_10 (not_10_out, C);
  not not_11 (not_11_out, C);
  and and_6 (and_6_out, not_11_out, not_12_out);
  not not_12 (not_12_out, B);
  not not_13 (not_13_out, B);
  and and_7 (and_7_out, not_13_out, not_14_out);
  not not_14 (not_14_out, A);
  not not_15 (not_15_out, D);
  and and_8 (and_8_out, not_15_out, B, A);
  not not_16 (not_16_out, D);
  and and_9 (and_9_out, not_16_out, not_17_out);
  not not_17 (not_17_out, B);
  not not_18 (not_18_out, D);
  and and_10 (and_10_out, not_18_out, A);
  not not_19 (not_19_out, B);
  and and_11 (and_11_out, not_19_out, A);
  not not_20 (not_20_out, D);
  and and_12 (and_12_out, not_20_out, C);
  and and_13 (and_13_out, D, not_21_out);
  not not_21 (not_21_out, C);
  not not_22 (not_22_out, C);
  and and_14 (and_14_out, not_22_out, not_23_out);
  not not_23 (not_23_out, A);
  not not_24 (not_24_out, C);
  and and_15 (and_15_out, not_24_out, B);
  and and_16 (and_16_out, B, not_25_out);
  not not_25 (not_25_out, A);
  and and_17 (and_17_out, C, not_26_out, A);
  not not_26 (not_26_out, B);
  not not_27 (not_27_out, C);
  and and_18 (and_18_out, not_27_out, not_28_out);
  not not_28 (not_28_out, A);
  and and_19 (and_19_out, B, not_29_out);
  not not_29 (not_29_out, A);
  and and_20 (and_20_out, D, C, not_30_out);
  not not_30 (not_30_out, B);
  not not_31 (not_31_out, B);
  and and_21 (and_21_out, not_31_out, not_32_out);
  not not_32 (not_32_out, A);
  and and_22 (and_22_out, C, not_33_out);
  not not_33 (not_33_out, B);
  and and_23 (and_23_out, C, not_34_out);
  not not_34 (not_34_out, A);
  and and_24 (and_24_out, D, not_35_out);
  not not_35 (not_35_out, B);
  not not_36 (not_36_out, D);
  and and_25 (and_25_out, not_36_out, not_37_out, B);
  not not_37 (not_37_out, C);
  not not_38 (not_38_out, D);
  and and_26 (and_26_out, not_38_out, C, not_39_out);
  not not_39 (not_39_out, B);
  and and_27 (and_27_out, C, B, not_40_out);
  not not_40 (not_40_out, A);
  not not_41 (not_41_out, C);
  and and_28 (and_28_out, D, not_41_out, not_42_out);
  not not_42 (not_42_out, B);
  not not_43 (not_43_out, B);
  and and_29 (and_29_out, D, not_43_out, A);
  or or_1 (a_2, and_1_out, and_2_out, and_3_out, and_4_out);
  or or_2 (b_2, and_5_out, and_6_out, and_7_out, and_8_out);
  or or_3 (c_2, and_9_out, and_10_out, and_11_out, and_12_out, and_13_out);
  or or_4 (d_2, and_14_out, and_15_out, and_16_out, and_17_out);
  or or_5 (e, and_18_out, and_19_out, and_20_out);
  or or_6 (f, and_21_out, and_22_out, and_23_out, and_24_out);
  or or_7 (g, and_25_out, and_26_out, and_27_out, and_28_out, and_29_out);
endmodule
