// Logisim project 152120241075_Q3.circ as structural Verilog: 1 circuit, main circuit main
module main (
  input  A1,
  input  A0,
  input  B1,
  input  B0
);

  wire n74154_1_p7, n74154_1_p8, n74154_1_p9, n74154_1_p10, n74154_1_p11, n74154_1_p12, n74154_1_p13,
       n74154_1_p14, n74154_1_p15, n74154_1_p16, n74154_1_p17, n74154_1_p18, n74154_1_p19, n74154_1_p20,
       n74154_1_p21, n74154_1_p22, nand_1_out, nand_2_out;

  // _74154 74154_1: pin names not known; wires that end beside it: 1'b0, 1'b0, A0, A1, B0, B1, n74154_1_p7, n74154_1_p8, n74154_1_p9, n74154_1_p10, n74154_1_p11, n74154_1_p12, n74154_1_p13, n74154_1_p14, n74154_1_p15, n74154_1_p16, n74154_1_p17, n74154_1_p18, n74154_1_p19, n74154_1_p20, n74154_1_p21, n74154_1_p22
  nand nand_1 (nand_1_out, n74154_1_p8, n74154_1_p10, n74154_1_p11, n74154_1_p13, n74154_1_p16, n74154_1_p18, n74154_1_p19, n74154_1_p21);
  LED led_1 (.in(nand_2_out));
  LED led_2 (.in(nand_1_out));
  nand nand_2 (nand_2_out, n74154_1_p7, n74154_1_p9, n74154_1_p12, n74154_1_p14, n74154_1_p15, n74154_1_p17, n74154_1_p20, n74154_1_p22);

  // Notes on the sheet:
  //   Z1
  //   Z2
endmodule
